# Fritzing sketch Arduino-NeoPixels-proto (saved by Fritzing 0.9.2b)
breadboards: 1

parts:
  Part1 = NeoPixel Jewel [part_number=2226]
  Part2 = 24 NeoPixel Ring [part_number=1586]
  Part3 = 16 NeoPixel Ring [part_number=1463]
  Part4 = Arduino Uno (Rev3)
  JACK1 = 2.1mm Barrel Jack with Terminal Block
  C1 = Electrolytic Capacitor [capacitance=1mF voltage=16V package="100 mil [THT, electrolytic]"]
  R2 = Resistor [tolerance=±5% resistance=470 package="2512 [SMD]"]

nets:
  GND: Part1.GND, Part2.GND, Part3.GND, Part4.GND, JACK1.NEG, C1.-
  N1: Part1.IN, Part4.D6_PWM, R2.Pin_0, R2.Pin_1
  N2: Part1.OUT, Part3.IN
  VDD: Part1.VDD, Part2.VDD, Part3.VDD, JACK1.POS, C1.+
  N3: Part2.IN, Part3.OUT

custom parts:
  NeoPixel Jewel: We fit seven of our tiny 5050 (5mm x 5mm) smart RGB LEDs onto a beautiful, round PCB with mounting holes and a chainable design to create what we think is our most elegant (and evening-wear appropriate) NeoPixel board yet. Use only one microcontroller pin to control as many as you can chain together! Each LED is addressable as the driver chip is inside the LED. Each one has ~18mA constant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
  24 NeoPixel Ring: 24 ultra bright smart LED NeoPixels are arranged in a circle with 2.6" (66mm) outer diameter. The rings are 'chainable' - connect the output pin of one to the input pin of another. Use only one microcontroller pin to control as many as you can chain together! Each LED is addressable as the driver chip is inside the LED. Each one has ~18mA constant current drive so the color will be very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
  16 NeoPixel Ring: 16 ultra bright smart LED NeoPixels are arranged in a circle with 1.75" (44.5mm) outer diameter. The rings are 'chainable' - connect the output pin of one to the input pin of another. Use only one microcontroller pin to control as many as you can chain together! Each LED is addressable as the driver chip is inside the LED. Each one has ~18mA constant current drive so the color will be very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

// code stored in the sketch: turnonpixel.ino
/*
  Turning a NeoPixel's Pixel On.

  This sketch is used to turn Pixels on or off, test them or set a lighting sequence of NeoPixel
  [1] strips or rings.

  SuperScanner project (GPL-2.0) [2] uses this sketch to light up a sample under a microscope with
  one NeoPixel at a time according to the computational imaging technique Fourier Ptychography.

  Created on February 2nd, 2018
  by Jose David Marroquin Toledo

  Modified on March 4th, 2018
  by Jose David Marroquin Toledo

  [1] https://github.com/adafruit/Adafruit_NeoPixel

  [2] https://github.com/josemarroquintoledo/superscanner-software-s3
  
*/

#include <Adafruit_NeoPixel.h>
#ifdef __AVR__
  #include <avr/power.h>
#endif

#define PIN 6
#define MAX_NUM_OF_PIXELS 47

struct pixel {
  int number = -1;
  int brightness = 0;
};

// From the strandtest example sketch (LGPL-3.0) by Adafruit
//
// Parameter 1 = number of pixels in strip
// Parameter 2 = Arduino pin number (most are valid)
// Parameter 3 = pixel type flags, add together as needed:
//   NEO_KHZ800  800 KHz bitstream (most NeoPixel products w/WS2812 LEDs)
//   NEO_KHZ400  400 KHz (classic 'v1' (not v2) FLORA pixels, WS2811 drivers)
//   NEO_GRB     Pixels are wired for GRB bitstream (most NeoPixel products)
//   NEO_RGB     Pixels are wired for RGB bitstream (v1 FLORA pixels, not v2)
//   NEO_RGBW    Pixels are wired for RGBW bitstream (NeoPixel RGBW products)
Adafruit_NeoPixel strip = Adafruit_NeoPixel(MAX_NUM_OF_PIXELS, PIN, NEO_RGBW + NEO_KHZ800);

// IMPORTANT: To reduce NeoPixel burnout risk, add 1000 uF capacitor across
// pixel power leads, add 300 - 500 Ohm resistor on first pixel's data input
// and minimize distance between Arduino and first pixel.  Avoid connecting
// on a live circuit...if you must, connect GND first.
//

// Custom lighting sequence obtained with setLightingSequence() (int).
const int PIXEL_SEQ[MAX_NUM_OF_PIXELS] =  {1, 4, 5, 6, 7, 2, 3, 14, 13, 12, 11, 10, 9, 8, 23, 22,
                                           21, 20, 19, 18, 17, 16, 15, 28, 29, 30, 31, 32, 33, 34,
                                           35, 36, 37, 38, 39, 40, 41, 42, 43, 44, 45, 46, 47, 24,
                                           25, 26, 27};

pixel lastPixel;
String incomingSerialData;
int commaIdx;  // Index number of the comma (',') in the main loop.
bool useCustomSeq = false; 
//
int sequenceStack[MAX_NUM_OF_PIXELS];

void setup() {
  // This is for Trinket 5V 16MHz, you can remove these three lines if you are not using a Trinket
  #if defined (__AVR_ATtiny85__)
    if (F_CPU == 16000000) clock_prescale_set(clock_div_1);
  #endif
  // End of trinket special code

  strip.begin();
  strip.show();
  Serial.begin(9600);
  Serial.println("<ArduinoReady>");
}

void loop() {
  if (Serial.available() > 0) {
    incomingSerialData = Serial.readString();
    incomingSerialData.trim();
    commaIdx = incomingSerialData.indexOf(',');
    if (commaIdx != -1) {
      int firstNum = incomingSerialData.substring(0, commaIdx + 1).toInt();
      int secondNum = incomingSerialData.substring(commaIdx + 1).toInt();
      if (firstNum > 0 && firstNum <= MAX_NUM_OF_PIXELS && secondNum >= 0 && secondNum <= 255) {
        // firstNum (int) equals 0 is also the value for non-numeric strings.
        lastPixel.number = incomingSerialData.substring(0, commaIdx + 1).toInt();
        lastPixel.brightness = incomingSerialData.substring(commaIdx + 1).toInt();
        if (useCustomSeq) {
          colorWipe(PIXEL_SEQ[lastPixel.number - 1], lastPixel.brightness);
        } else {
          colorWipe(lastPixel.number, lastPixel.brightness);
        }
      }
    } else {
      incomingSerialData.toLowerCase();
      if (incomingSerialData.compareTo("useseq") == 0 && !useCustomSeq) {
        Serial.println("<CustomSeqUse>");
        useCustomSeq = true;
      } if (incomingSerialData.compareTo("noseq") == 0 && useCustomSeq) {
        Serial.println("<CustomSeqNo>");
        useCustomSeq = false;
      } else if (incomingSerialData.compareTo("clear") == 0) {
        turnAllOff();  // Turn all Pixels off.
      } else if (incomingSerialData.compareTo("test") == 0) {
        // It uses the custom lighting sequence PIXEL_SEQ[] (const int).
        if (!useCustomSeq) {
          Serial.println("<CustomSeqUse>");
          useCustomSeq = true;
        }
        testPixels();
      } else if (incomingSerialData.compareTo("setseq") == 0) {
        if (useCustomSeq) {
          Serial.println("<CustomSeqNo>");
          useCustomSeq = false;
        }
        setLightingSequence(); 
      }
    }
  }
}

void initSequenceStack() {
  for (int i = 0; i < MAX_NUM_OF_PIXELS; i++) {
    sequenceStack[i] = -1;
  }  
}

// Gives a preview of the lighting sequence.
void showSequence(int currentPixelIdx, int currentPixelBrightness) {
  const int BRIGHTNESS_LEVEL = 31;
  const int DELAY_TIME = 300;
  Serial.println("<SequencePreviewStart>");
  for (int i = 0; i <= currentPixelIdx; i++) {
    delay(DELAY_TIME);
    colorWipe(sequenceStack[i], BRIGHTNESS_LEVEL);
  }
  delay(DELAY_TIME * 4);
  // Turn the Pixel off 
  for (int i = 0; i <= currentPixelIdx; i++) {
    colorWipe(sequenceStack[i], 0);
  }
  Serial.println("<SequencePreviewEnd>");
  printLightingSeq();
}

// Prints the lighting sequence set by the user. Commands: f ("forward") to go to the next Pixel,
// b ("backward") to go to the previous Pixel, jf ("jump forward") to go JUMP_STEPS (int) forward,
// jb ("jump backward") to go JUMP_STEPS (int) backward and q ("quit") to exit.
int setLightingSequence() {
  const int BRIGHTNESS_LEVEL = 31;
  const int JUMP_STEPS = 5;
  int currentPixel = 1;
  int stackPtr = -1;
  String incomingData;
  int prevPixel;
  bool inSeq;
  Serial.println("<StripSetSequence>");
  initSequenceStack();
  turnAllOff();
  colorWipe(currentPixel, BRIGHTNESS_LEVEL);  // Turn the first Pixel on.
  while (true) {
    if (Serial.available() > 0) {
      incomingData = Serial.readString();
      incomingData.trim();
      incomingData.toLowerCase();
      if (incomingData.compareTo("f") == 0 && currentPixel < MAX_NUM_OF_PIXELS) {
        Serial.println("<StripForward>");
        prevPixel = currentPixel;
        currentPixel++;  // Go to the next Pixel in the strip.
        colorWipe(prevPixel, 0);  // Turn the previous Pixel off.
        colorWipe(currentPixel, BRIGHTNESS_LEVEL);  // Turn the current Pixel on.
      } else if (incomingData.compareTo("jf") == 0) {
        Serial.println("<StripJumpForward-" + String(JUMP_STEPS) + '>');
        prevPixel = currentPixel;
        currentPixel = currentPixel + JUMP_STEPS;
        if (currentPixel >= MAX_NUM_OF_PIXELS - 1) {
          // Go to the last Pixel in the strip.
          currentPixel = MAX_NUM_OF_PIXELS - 1;
        }
        colorWipe(prevPixel, 0);  // Turn the previous Pixel off.
        colorWipe(currentPixel, BRIGHTNESS_LEVEL);  // Turn the current Pixel on.
      } else if (incomingData.compareTo("b") == 0 && currentPixel > 1) {
        Serial.println("<StripBack>");
        prevPixel = currentPixel;
        currentPixel--;  // Go to previous Pixel in the strip.
        colorWipe(prevPixel, 0);  // Turn the previous Pixel off.
        colorWipe(currentPixel, BRIGHTNESS_LEVEL);  // Turn the current Pixel on.
      } else if (incomingData.compareTo("jb") == 0) {
        Serial.println("<StripJumpBack-" + String(JUMP_STEPS) + '>');
        prevPixel = currentPixel;
        currentPixel = currentPixel - JUMP_STEPS;
        if (currentPixel < 1) {
          // Go to the first Pixel in the strip.
          currentPixel = 1;
        }
        colorWipe(prevPixel, 0);  // Turn the previous Pixel off.
        colorWipe(currentPixel, BRIGHTNESS_LEVEL);  // Turn the current Pixel on.
      } else if (incomingData.compareTo("push") == 0) {
        inSeq = false;
        // Look for the current Pixel in the sequence to add it only if it does not exist.
        for (int i = 0; i <= stackPtr; i++) {
          if (sequenceStack[i] == currentPixel) {
            inSeq = true;
            break;
          }
        }
        if (!inSeq) {
          Serial.println("<SequencePixelPush-" + String(currentPixel) + ">");
          // Give to the element referenced by stackPtr (int) in the sequenceStack array the value
          // of the position of the current Pixel.
          stackPtr++;
          sequenceStack[stackPtr] = currentPixel;
          printLightingSeq(); 
        }          
      } else if (incomingData.compareTo("pop") == 0 && stackPtr > -1) {
        Serial.println("<SequencePop>");
        // Clear the value of the element referenced by stackPtr (int) in the sequenceStack array.
        sequenceStack[stackPtr] = -1;
        stackPtr--;
        printLightingSeq();
      } else if (incomingData.compareTo("show") == 0) {
        colorWipe(currentPixel, 0);  // Turn the current Pixel off.
        showSequence(stackPtr, BRIGHTNESS_LEVEL);
        colorWipe(currentPixel, BRIGHTNESS_LEVEL);  // Turn the current Pixel on again.
      } else if (incomingData.compareTo("print") == 0) {
        printLightingSeq();
      } else if (incomingData.compareTo("q") == 0) {
        Serial.println("<StripSetSequenceQuit>");
        printLightingSeq();
        turnAllOff();
        return 0;
      }
    }
  }
}

// Prints the lighting sequence as array to copy and paste in an Arduino code.
void printLightingSeq() {
  Serial.print('{');
  for (int i = 0; i < MAX_NUM_OF_PIXELS; i++) {
    if (sequenceStack[i] != -1) {
      if (i > 0) {
        Serial.print(", ");
      }
      Serial.print(sequenceStack[i]);
    }
  }
  Serial.println('}');
}

// Turns a Pixel on with the white color or turns it off.
//
// pixel (uint16_t) is the Pixel's index in the strip from 1 to MAX_NUM_OF_PIXELS.
void colorWipe(uint16_t pixel, int brightness) {
  strip.setPixelColor(pixel - 1, 0, 0, 0, brightness);
  strip.show();
  if (brightness > 0) {
    Serial.println("<Arduino-PixelOn-" + String(pixel) + ">");
  } else {
    Serial.println("<Arduino-PixelOff-" + String(pixel) + ">");
  }
}

// Turns all pixels (MAX_NUM_OF_PIXELS) off.
void turnAllOff() {
  Serial.println("<StripTurnOff>");
  for (int i = 1; i <= MAX_NUM_OF_PIXELS; i++) {
    colorWipe(i, strip.Color(0, 0, 0, 0));
  }
  Serial.println("<StripTurnedOff>");
}

// Launches a test routine for all Pixels (MAX_NUM_OF_PIXELS).
void testPixels() {
  const int DELAY_TIME = 150;  // In miliseconds.
  const int BRIGHTNESS_LEVEL = 31;
  Serial.println("<StripTestStart>");
  turnAllOff();
  delay(DELAY_TIME);
  // Turn one Pixel on at a time and maintains it.
  for (int i = 0; i < MAX_NUM_OF_PIXELS; i++) {
    colorWipe(PIXEL_SEQ[i], BRIGHTNESS_LEVEL);
    delay(DELAY_TIME);
  }
  // Turn one Pixel off at a time.
  for (int i = MAX_NUM_OF_PIXELS - 1; i >= 0; i--) {
    colorWipe(PIXEL_SEQ[i], 0);
    delay(DELAY_TIME);
  }
  for (int k = 0; k < 3; k++) {
    if (k % 2 != 0) {
      // Decrease the brightness level from brightness (int) to 0 of each Pixel.
      for (int i = BRIGHTNESS_LEVEL; i >= 0; i = i - 3) {
        for (int j = MAX_NUM_OF_PIXELS - 1; j >= 0; j--) {
          colorWipe(PIXEL_SEQ[j], i);
        }
      }    
    } else {
      // Increase the brightness level from 0 to brightness (int) of each Pixel.
      for (int i = 0; i < BRIGHTNESS_LEVEL + 1; i = i + 3) {
        for (int j = 0; j < MAX_NUM_OF_PIXELS; j++) {
          colorWipe(PIXEL_SEQ[j], i);
        }
      }
    }
  }
  Serial.println("<StripTestEnd>");
}
